# Fritzing sketch sketch (saved by Fritzing 0.9.3b)
breadboards: 1

parts:
  WeMos_D1_Mini2 = WeMos D1 Mini
  U1 = WS2812 RGB LED strip
  S1 = Square Pushbutton
  DHT1 = DHT22 Humidity and Temperature Sensor
  R1 = Resistor [tolerance=±5% resistance=10k package="2512 [SMD]"]
  R2 = Photocell (LDR) [package=THT]
  R3 = Resistor [tolerance=±5% resistance=10k package="2512 [SMD]"]

nets:
  N1: WeMos_D1_Mini2.3V3, R2.pin_1
  5V: WeMos_D1_Mini2.5V, U1.VCC, DHT1.VDD, DHT1.DATA, R1.Pin_1
  N2: WeMos_D1_Mini2.A0, R2.pin_0, R3.Pin_0
  N3: WeMos_D1_Mini2.D3, U1.DIN
  N4: WeMos_D1_Mini2.D4, S1.leg0
  N5: WeMos_D1_Mini2.D5, R1.Pin_0
  GND: WeMos_D1_Mini2.G, U1.GND, S1.leg1, DHT1.GND, R3.Pin_1

custom parts:
  WeMos D1 Mini: The D1 mini is a mini wifi board based on ESP-8266EX.
  WS2812 RGB LED strip: WS2812 strip
